// Logisim project CRC_flipflop_GenRemainder.circ as structural Verilog: 1 circuit, main circuit main
module main (
  input  INPUT,
  input  CLOCK,
  input  CLEAR,
  output LSB,
  output out_5,
  output out_6,
  output MSB,
  output MSB_2,
  output out_9,
  output out_10,
  output LSB_2
);

  wire not_1_out, not_2_out, not_3_out, not_4_out, xor_1_out, xor_2_out;

  xor xor_1 (xor_1_out, MSB, INPUT);
  not not_1 (not_1_out, xor_1_out);
  xor xor_2 (xor_2_out, MSB, LSB);
  J_K_Flip_Flop #(.trigger("falling")) u_LSB (
    .J(xor_1_out), .clk(CLOCK), .K(not_1_out), .Q(LSB), .preset(1'b0), .en(1'b1), .reset(CLEAR));  // open: Qn
  J_K_Flip_Flop #(.trigger("falling")) j_k_ff_1 (
    .J(xor_2_out), .clk(CLOCK), .K(not_2_out), .Q(out_5), .preset(1'b0), .en(1'b1), .reset(CLEAR));  // open: Qn
  not not_2 (not_2_out, xor_2_out);
  J_K_Flip_Flop #(.trigger("falling")) j_k_ff_2 (
    .J(out_5), .clk(CLOCK), .K(not_3_out), .Q(out_6), .preset(1'b0), .en(1'b1), .reset(CLEAR));  // open: Qn
  not not_3 (not_3_out, out_5);
  not not_4 (not_4_out, out_6);
  J_K_Flip_Flop #(.trigger("falling")) u_MSB (
    .J(out_6), .clk(CLOCK), .K(not_4_out), .Q(MSB), .preset(1'b0), .en(1'b1), .reset(CLEAR));  // open: Qn

  assign LSB_2 = LSB;
  assign MSB_2 = MSB;
  assign out_9 = out_6;
  assign out_10 = out_5;

  // Notes on the sheet:
  //   Look me here ->
  //   Remainder
endmodule
